# Fritzing sketch Booster w missing pulse detection (saved by Fritzing 0.8.5b)
circuit board: 8.68463cm x 4.6977cm
breadboards: 1

parts:
  R3 = Resistor [tolerance=±5% resistance=10k package=THT]
  C2 = Ceramic Capacitor [capacitance=100nF package="200 mil [THT, multilayer]"]
  4xAND1 = quad 2-input AND gate [chip_label=4xAND package="DIP (Dual Inline) [THT]"]
  R2 = Resistor [tolerance=±5% resistance=100 package=THT]
  C4 = Electrolytic Capacitor [capacitance=0.47mF voltage=35V package="300 mil [THT, electrolytic]"]
  R1 = Resistor [tolerance=±5% resistance=100 package=THT]
  U2 = SN74LS14N [package="DIP14 [THT]"]
  C3 = SKB B40 C1400 [package=G3]
  R4 = Resistor [tolerance=±5% resistance=10k package=THT]
  J3 = screw terminal, 2 pins
  J4 = Screw terminal - 2 pins [package=THT]
  J1 = screw terminal, 3 pins
  5205 = TLE 5205-2S [package=TDO220]
  C1 = Ceramic Capacitor [capacitance=100nF package="200 mil [THT, multilayer]"]
  D1 = Rectifier Diode [part_number=1N4001 package="300 mil [THT]"]
  D2 = Rectifier Diode [part_number=1N4001 package="300 mil [THT]"]
  R5 = Resistor [tolerance=±5% resistance=0 package=THT]
  R6 = Resistor [tolerance=±5% resistance=220 package=THT]

nets:
  N1: R3.Pin_0, C2.1, 4xAND1.pin2, R2.Pin_1
  GND: R3.Pin_1, C2.0, 4xAND1.pin7, C4.-, U2.GND, C3.4, R4.Pin_1, J1.pin3, 5205.4, C1.0
  N2: 4xAND1.pin1, R1.Pin_1, R4.Pin_0, C1.1
  N3: 4xAND1.pin3, 4xAND1.pin9, R6.Pin_1
  N4: 4xAND1.pin8, 5205.3
  N5: 4xAND1.pin10, U2.1A, U2.3A, J1.pin2
  N6: 4xAND1.pin11, 5205.5
  N7: 4xAND1.pin12, R6.Pin_0
  N8: 4xAND1.pin13, U2.1Y, U2.2A
  N9: 4xAND1.pin14, R5.Pin_0
  N10: R2.Pin_0, D1.cathode
  N11: C4.+, C3.2, 5205.6
  N12: R1.Pin_0, D2.cathode
  N13: U2.2Y, D2.anode
  N14: U2.3Y, D1.anode
  5V: U2.VCC, J1.pin1, R5.Pin_1
  N15: C3.1, J4.pin1
  N16: C3.3, J4.pin2
  N17: J3.pin1, 5205.7
  N18: J3.pin2, 5205.1

notes:
  Betriebsspannung (5V)
  GPIO / TTL
  Masse / Ground
  Spannungsversorgung
  ca. 15V = oder ~
  zum Gleis

custom parts:
  quad 2-input AND gate: IC with 4 2-input AND gates
