# Fritzing sketch Booster (saved by Fritzing 0.9.3b)
circuit board: 5.42376cm x 4.93471cm
breadboards: 1

parts:
  74HC08 = IC, DIP package, 14 pins [chip_label=4xAND]
  74HC14 = IC, DIP package, 14 pins [chip_label=3xNOT]
  R1 = Resistor [tolerance=±5% resistance=4.7k package=THT]
  R2 = Resistor [tolerance=±5% resistance=4.7k package=THT]
  +5V_IN_OUT_GND = screw terminal, 4 pins
  D1 = Rectifier Diode [part_number=1N4001 package="300 mil [THT]"]
  R3 = Resistor [tolerance=±5% resistance=330 package=THT]
  D2 = Rectifier Diode [part_number=1N4001 package="300 mil [THT]"]
  R4 = Resistor [tolerance=±5% resistance=330 package=THT]
  C1 = Electrolytic Capacitor [capacitance=1mF voltage=35V package="300 mil [THT, electrolytic]"]
  12V~ = screw terminal, 3 pins
  DCC = screw terminal, 3 pins
  G1 = SKB B40 C1400 [package=G3]
  TLE_5205 = TLE 5205 H-Bridge [package=P-TO220-7-11]
  C2 = Electrolytic Capacitor [capacitance=4.7µF package="100 mil [THT, electrolytic]"]
  C3 = Electrolytic Capacitor [capacitance=4.7µF package="100 mil [THT, electrolytic]"]

nets:
  N1: 74HC08.pin1, 74HC14.pin1, 74HC14.pin13, +5V_IN_OUT_GND.pin3
  N2: 74HC08.pin2, 74HC08.pin6, 74HC14.pin9
  N3: 74HC08.pin3, TLE_5205.IN2
  N4: 74HC08.pin4, R1.Pin_1, D1.cathode, C2.+
  N5: 74HC08.pin5, R2.Pin_1, D2.cathode, C3.+
  GND: 74HC08.pin7, 74HC14.pin7, R1.Pin_0, R2.Pin_0, +5V_IN_OUT_GND.pin1, C1.-, G1.4, TLE_5205.GND, C2.-, C3.-
  N6: 74HC08.pin14, 74HC14.pin14, +5V_IN_OUT_GND.pin4
  N7: 74HC14.pin2, R3.Pin_1
  N8: 74HC14.pin8, TLE_5205.IN1
  N9: 74HC14.pin10, R4.Pin_0
  N10: 74HC14.pin11, 74HC14.pin12
  N11: +5V_IN_OUT_GND.pin2, TLE_5205.EF
  N12: D1.anode, R3.Pin_0
  N13: D2.anode, R4.Pin_1
  N14: C1.+, G1.2, TLE_5205.V_S
  N15: 12V~.pin1, G1.3
  N16: 12V~.pin2, G1.1
  N17: DCC.pin1, TLE_5205.OUT1
  N18: DCC.pin2, TLE_5205.OUT2

notes:
  SRSoftware
  Booster v3
  EF
  GND
  V+
  1
  2

custom parts:
  TLE 5205 H-Bridge: The TLE 5205-2 is an integrated power H-bridge with DMOS output stages for driving DC-Motors. Operation modes forward (cw), reverse (ccw), brake and high impedance are invoked from just two control pins with TTL/CMOS compatible levels.
