# Fritzing sketch booster (saved by Fritzing 0.8.5b)
circuit board: 6.49142cm x 3.07908cm
breadboards: 1

parts:
  R2 = Resistor [tolerance=±5% resistance=4.7k package=THT]
  Q1 = PNP-Transistor [package="TO92 [THT]"]
  D1 = Rectifier Diode [part_number=1N4001 package="300 mil [THT]"]
  R3 = Resistor [tolerance=±5% resistance=100 package=THT]
  R4 = Resistor [tolerance=±5% resistance=2.7k package=THT]
  Q2 = NPN-Transistor [package="TO92 [THT]"]
  R5 = Resistor [tolerance=±5% resistance=4.7k package=THT]
  R6 = Resistor [tolerance=±5% resistance=10k package=THT]
  5205 = TLE 5205-2S [package=TDO220]
  C1 = Ceramic Capacitor [capacitance=470nF voltage=100V package="200 mil [THT, multilayer]"]
  R7 = Resistor [tolerance=±5% resistance=27k package=THT]
  J2 = screw terminal, 3 pins
  J3 = screw terminal, 4 pins

nets:
  N1: R2.Pin_0, R7.Pin_1, J2.pin2
  N2: R2.Pin_1, Q1.B
  5V: Q1.E, J2.pin3
  N3: Q1.C, D1.anode, R5.Pin_1, 5205.3
  N4: D1.cathode, R3.Pin_0
  N5: R3.Pin_1, R4.Pin_1, C1.0
  N6: R4.Pin_0, Q2.C, R6.Pin_1, 5205.5
  GND: Q2.E, R6.Pin_0, 5205.4, C1.1, R7.Pin_0, J2.pin1, J3.pin3
  N7: Q2.B, R5.Pin_0
  N8: 5205.1, J3.pin4
  20V: 5205.6, J3.pin2
  N9: 5205.7, J3.pin1
